// Digital circuit memory_Module.dig as structural Verilog
module memory_Module (
  input  [3:0] Address,
  input  [3:0] Data,
  input  Read,
  input  Write,
  input  clock,
  output [3:0] data_2
);

  Register #(.Bits(4)) register_1 (.D(Address), .C(clock), .en(Read), .Q(data_2));
endmodule
